# Fritzing sketch Codeschloss_Teil_1 (saved by Fritzing 0.9.3b)
breadboards: 1

parts:
  Nano_V1 = Nano V3
  LED2 = RGB LED (com. cathode, rgb) [package="5 mm [THT]"]
  R1 = Resistor [tolerance=±5% resistance=100 package="0805 [SMD]"]
  R2 = Resistor [tolerance=±5% resistance=100 package="0805 [SMD]"]
  R3 = Resistor [tolerance=±5% resistance=100 package="0805 [SMD]"]
  U2 = 2-Channel 5v Relay Shield [package=relay-2ch5v10a]
  Matrix_keypad2 = KEYPAD 4x4

nets:
  GND: Nano_V1.GND, LED2.common_cathode, U2.GND
  N1: Nano_V1.D2, R2.Pin_1
  N2: Nano_V1.D3, R1.Pin_1
  N3: Nano_V1.D4, R3.Pin_1
  N4: Nano_V1.D5, Matrix_keypad2.row4
  N5: Nano_V1.D6, Matrix_keypad2.row3
  N6: Nano_V1.D7, Matrix_keypad2.row2
  N7: Nano_V1.D8, Matrix_keypad2.row1
  N8: Nano_V1.D9, Matrix_keypad2.col4
  N9: Nano_V1.D10, Matrix_keypad2.col3
  N10: Nano_V1.D11/MOSI, Matrix_keypad2.col2
  N11: Nano_V1.D12/MISO, Matrix_keypad2.col1
  5V: Nano_V1.5V, U2.VCC
  N12: Nano_V1.A0, U2.IN1
  N13: LED2.red_anode, R1.Pin_0
  N14: LED2.green_anode, R2.Pin_0
  N15: LED2.blue_anode, R3.Pin_0

custom parts:
  Nano V3: Can be used universally thanks to a compact design! By 14 digital in - and outputs and 6 analog inputs on the Nano V3 can also be used for larger projects! Thanks to the ATmega328 micro-controller, as well as more sophisticated programs to be executable! By Arduino compatibility in the Arduino IDE programmable! With FTDI Chip! Usual high quality and fast delivery directly from Germany by order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
  2-Channel 5v Relay Shield: 2 Channel 5v Relay Shield w. 2x SPD-06VDC-SD-C
  KEYPAD 4x4: Matrix keypad 16 buttons, 4 rows x 4 columns
