# Fritzing sketch Codeschloss_Teil_6 (saved by Fritzing 0.9.3b)
breadboards: 1

parts:
  Nano_V1 = Nano V3
  LED2 = RGB LED (com. cathode, rgb) [package="5 mm [THT]"]
  R1 = Resistor [tolerance=±5% resistance=100 package="0805 [SMD]"]
  R2 = Resistor [tolerance=±5% resistance=100 package="0805 [SMD]"]
  R3 = Resistor [tolerance=±5% resistance=100 package="0805 [SMD]"]
  U2 = 2-Channel 5v Relay Shield [package=relay-2ch5v10a]
  Matrix_keypad2 = KEYPAD 4x4
  Nano_V2 = Nano V3
  J1 = Piezo Speaker
  U3 = Sharp PC817 [package=THT]
  U4 = Sharp PC817 [package=THT]
  R4 = Resistor [tolerance=±1% resistance=1k package=THT]
  R5 = Resistor [tolerance=±1% resistance=1k package=THT]
  R6 = Resistor [tolerance=±5% resistance=220 package=THT]
  R7 = Resistor [tolerance=±5% resistance=220 package=THT]
  ENC28J1 = ENC28J60

nets:
  GND: Nano_V1.GND, LED2.common_cathode, U2.GND, Nano_V2.GND, J1.pin1, R4.Pin_0, R5.Pin_0, R6.Pin_0, R7.Pin_0, ENC28J1.GND
  N1: Nano_V1.D2, Matrix_keypad2.row4
  N2: Nano_V1.D3, Matrix_keypad2.row3
  N3: Nano_V1.D4, Matrix_keypad2.row2
  N4: Nano_V1.D5, Matrix_keypad2.row1
  N5: Nano_V1.D6, Matrix_keypad2.col4
  N6: Nano_V1.D7, Matrix_keypad2.col3
  N7: Nano_V1.D8, Matrix_keypad2.col2
  N8: Nano_V1.D9, R3.Pin_1
  N9: Nano_V1.D10, R2.Pin_1
  N10: Nano_V1.D11/MOSI, R1.Pin_1
  N11: Nano_V1.D12/MISO, U4.Pin_3, R4.Pin_1
  5V: Nano_V1.5V, U2.VCC, Nano_V2.5V, U3.Pin_4, U4.Pin_4, ENC28J1.5v
  N12: Nano_V1.A2, U3.Pin_1
  N13: Nano_V1.A1, J1.pin2
  N14: Nano_V1.A0, Matrix_keypad2.col1
  N15: LED2.red_anode, R1.Pin_0
  N16: LED2.green_anode, R2.Pin_0
  N17: LED2.blue_anode, R3.Pin_0
  N18: U2.IN1, Nano_V2.A1
  N19: U2.IN2, Nano_V2.A0
  N20: Nano_V2.RESET, Nano_V2.D13/SCK, ENC28J1.SCK, ENC28J1.RST
  N21: Nano_V2.D3, U4.Pin_1
  N22: Nano_V2.D5, U3.Pin_3, R5.Pin_1
  N23: Nano_V2.D10, ENC28J1.CS
  N24: Nano_V2.D11/MOSI, ENC28J1.SI
  N25: Nano_V2.D12/MISO, ENC28J1.INT, ENC28J1.SO
  N26: U3.Pin_2, R7.Pin_1
  N27: U4.Pin_2, R6.Pin_1

custom parts:
  Nano V3: Can be used universally thanks to a compact design! By 14 digital in - and outputs and 6 analog inputs on the Nano V3 can also be used for larger projects! Thanks to the ATmega328 micro-controller, as well as more sophisticated programs to be executable! By Arduino compatibility in the Arduino IDE programmable! With FTDI Chip! Usual high quality and fast delivery directly from Germany by order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
  2-Channel 5v Relay Shield: 2 Channel 5v Relay Shield w. 2x SPD-06VDC-SD-C
  KEYPAD 4x4: Matrix keypad 16 buttons, 4 rows x 4 columns
  ENC28J60: Ethernet Module ENC28J60
